// Logisim project ram.circ as structural Verilog: 1 circuit, main circuit main
module main (
  input  [4:0] address,
  input  [3:0] Data_IN,
  input  Store,
  input  Clock,
  input  Load,
  output [3:0] Data_OUT
);

  wire or_1_out;
  wire [4:0] subtractor_1_out;

  Subtractor #(.width(5)) subtractor_1 (.a(address), .b(5'b01000), .out(subtractor_1_out), .bin(1'b0));  // open: bout
  or or_1 (or_1_out, address[3], address[4]);
  RAM #(.addrWidth(4), .dataWidth(4), .bus("separate")) ram_1 (
    .addr(subtractor_1_out[3:0]), .din(Data_IN), .data(Data_OUT), .str(Store), .sel(or_1_out), .clk(Clock),
    .ld(Load));  // open: clr
endmodule
